# Fritzing sketch WiringDiagram (saved by Fritzing 0.9.2b)
breadboards: 1

parts:
  IC1 = Fubarino Mini v1.5 [package="DIP (Dual Inline) [THT]"]  # not connected
  T1 = TMP36 Temperature Sensor [package="TO92 [THT]"]
  J1 = female pin header, 4 pins [form="♀ (female)"]
  Power_plug1 = Power plug
  LPD8806_RGB_LED_Strip3 = LPD8806 RGB LED Strip

nets:
  GND: T1.GND, J1.pin1, Power_plug1.GND, LPD8806_RGB_LED_Strip3.GND
  N1: J1.pin2, LPD8806_RGB_LED_Strip3.DI
  N2: J1.pin3, LPD8806_RGB_LED_Strip3.CI
  VCC: J1.pin4, Power_plug1.VCC, LPD8806_RGB_LED_Strip3.+5V

custom parts:
  Fubarino Mini v1.5: A chipKIT PIC32 based development board from Schmalz Haus LLC.
  LPD8806 RGB LED Strip: Digitally addressable RGB LED strip
